// Logisim project StackOrganization.circ as structural Verilog: 1 circuit, main circuit main
module main (
  input  [2:0] in_1,
  input  [2:0] in_2,
  input  in_3,
  input  Push,
  output [15:0] out_5
);

  wire and_1_out, and_2_out, clock_1_out, comparator_1_eq, comparator_2_eq, not_1_out, not_3_out, not_4_out,
       or_1_out;
  wire [2:0] counter_1_q;
  wire [15:0] counter_2_q;

  Comparator #(.width(3)) comparator_1 (.a(in_2), .b(counter_1_q), .eq(comparator_1_eq));  // open: gt, lt
  not not_1 (not_1_out, and_1_out);
  Comparator #(.width(3)) comparator_2 (.a(in_1), .b(counter_1_q), .eq(comparator_2_eq));  // open: gt, lt
  // NOT_Gate not_2 has open pins: in=not_3_out, out=open
  buf and_1 (and_1_out, comparator_2_eq);  // AND_Gate
  and and_2 (and_2_out, not_1_out, 1'b1);
  or or_1 (or_1_out, and_2_out, not_3_out);
  Clock clock_1 (.out(clock_1_out));
  Counter #(.width(3), .max('h7)) counter_1 (
    .load(not_3_out), .count(or_1_out), .Q(counter_1_q), .clk(clock_1_out));  // open: D, carry, clr
  not not_3 (not_3_out, Push);
  Counter #(.width(16), .max('hffff)) counter_2 (
    .count(in_3), .Q(counter_2_q), .clk(clock_1_out));  // open: load, D, carry, clr
  not not_4 (not_4_out, Push);
  RAM #(.addrWidth(3), .dataWidth(16), .bus("separate")) ram_1 (
    .addr(counter_1_q), .din(counter_2_q), .data(out_5), .clk(clock_1_out), .ld(not_4_out));  // open: str, sel, clr

  // Notes on the sheet:
  //   SP
  //   DR
endmodule
