// Logisim project alu.circ as structural Verilog: 1 circuit, main circuit main
module main (
  input  [3:0] in_1,
  input  in_2,
  input  in_3,
  input  [3:0] in_4,
  input  in_5,
  input  [1:0] in_6,
  input  [1:0] in_7,
  input  [3:0] in_8,
  output out_9
);

  wire adder_1_cout, adder_2_cout, adder_3_cout, multiplexer_1_out, multiplexer_2_out, multiplexer_3_out,
       multiplexer_4_out, not_1_out, not_2_out, not_3_out, not_4_out;
  wire [3:0] adder_1_out, and_1_out, multiplexer_5_out, not_5_out, or_1_out, shifter_1_out, shifter_2_out,
       xor_1_out;

  not not_1 (not_1_out, in_8[0]);
  not not_2 (not_2_out, in_8[1]);
  not not_3 (not_3_out, in_8[2]);
  not not_4 (not_4_out, in_8[3]);
  Multiplexer #(.select(2)) multiplexer_1 (
    .in0(in_5), .in1(in_8[0]), .in2(not_1_out), .in3(in_2), .out(multiplexer_1_out), .sel(in_6));  // open: en
  Multiplexer #(.select(2)) multiplexer_2 (
    .in0(in_5), .in1(in_8[1]), .in2(not_2_out), .in3(in_2), .out(multiplexer_2_out), .sel(in_6));  // open: en
  Multiplexer #(.select(2)) multiplexer_3 (
    .in0(in_5), .in1(in_8[2]), .in2(not_3_out), .in3(in_2), .out(multiplexer_3_out), .sel(in_6));  // open: en
  Multiplexer #(.select(2)) multiplexer_4 (
    .in0(in_5), .in1(in_8[3]), .in2(not_4_out), .in3(in_2), .out(multiplexer_4_out), .sel(in_6));  // open: en
  assign and_1_out = in_1 & in_8;  // AND_Gate and_1, 4 bits wide
  assign or_1_out = in_1 | in_8;  // OR_Gate or_1, 4 bits wide
  assign not_5_out = ~in_1;  // NOT_Gate not_5, 4 bits wide
  Shifter #(.width(4)) shifter_1 (.in(in_1), .\dist (2'b01), .out(shifter_1_out));
  Shifter #(.width(4), .shift("lr")) shifter_2 (.in(in_1), .\dist (2'b01), .out(shifter_2_out));
  assign xor_1_out = in_1 ^ in_8;  // XOR_Gate xor_1, 4 bits wide
  Adder #(.width(1)) adder_1 (
    .a(multiplexer_1_out), .b(in_1[0]), .out(adder_1_out[0]), .cin(in_3), .cout(adder_1_cout));
  Adder #(.width(1)) adder_2 (
    .a(multiplexer_2_out), .b(in_1[1]), .out(adder_1_out[1]), .cin(adder_1_cout), .cout(adder_2_cout));
  Adder #(.width(1)) adder_3 (
    .a(multiplexer_3_out), .b(in_1[2]), .out(adder_1_out[2]), .cin(adder_2_cout), .cout(adder_3_cout));
  Adder #(.width(1)) adder_4 (
    .a(multiplexer_4_out), .b(in_1[3]), .out(adder_1_out[3]), .cin(adder_3_cout), .cout(out_9));
  Multiplexer #(.select(2), .width(4)) multiplexer_5 (
    .in0(and_1_out), .in1(or_1_out), .in2(xor_1_out), .in3(not_5_out), .out(multiplexer_5_out), .sel(in_6));  // open: en
  Multiplexer #(.select(2), .width(4)) multiplexer_6 (
    .in0(adder_1_out), .in1(multiplexer_5_out), .in2(shifter_1_out), .in3(shifter_2_out), .out(in_4),
    .sel(in_7));  // open: en
endmodule
