// Logisim project booth_s algorithm.circ as structural Verilog: 1 circuit, main circuit main
module main (
  output [4:0] out_1,
  output [1:0] out_2
);

  wire Clock, counter_2_q, not_1_out, not_2_out, Shift, shift_register_2_out, shift_register_3_out, xor_1_out;
  wire [4:0] adder_1_out, multiplexer_1_out, shift_register_1_q4, shift_register_2_q4;

  Shift_Register #(.length(5)) shift_register_1 (
    .q0(shift_register_1_q4[4]), .q1(shift_register_1_q4[3]), .q2(shift_register_1_q4[2]),
    .q3(shift_register_1_q4[1]), .q4(shift_register_1_q4[0]));  // open: shift, in, clk, out, load, clr, d0, d1, d2, d3, d4
  Adder #(.width(5)) adder_1 (.a(shift_register_1_q4), .b(shift_register_2_q4), .out(adder_1_out));  // open: cin, cout
  Subtractor #(.width(5)) subtractor_1 (
    .a(shift_register_2_q4), .b(shift_register_1_q4), .out(out_1));  // open: bin, bout
  not not_1 (not_1_out, Shift);
  Shift_Register #(.length(5)) shift_register_2 (
    .shift(Shift), .in(shift_register_2_q4[4]), .clk(Clock), .out(shift_register_2_out), .load(not_1_out),
    .d0(multiplexer_1_out[4]), .q0(shift_register_2_q4[4]), .d1(multiplexer_1_out[3]),
    .q1(shift_register_2_q4[3]), .d2(multiplexer_1_out[2]), .q2(shift_register_2_q4[2]),
    .d3(multiplexer_1_out[1]), .q3(shift_register_2_q4[1]), .d4(multiplexer_1_out[0]),
    .q4(shift_register_2_q4[0]));  // open: clr
  Multiplexer #(.select(2), .width(5)) multiplexer_1 (
    .in0(shift_register_2_q4), .in1(adder_1_out), .in2(out_1), .in3(shift_register_2_q4),
    .out(multiplexer_1_out), .sel(out_2));  // open: en
  Shift_Register #(.length(5)) shift_register_3 (
    .shift(Shift), .in(shift_register_2_out), .clk(Clock), .out(shift_register_3_out), .q4(out_2[1]));  // open: load, clr, d0, q0, d1, q1, d2, q2, d3, q3, d4
  Shift_Register #(.length(1)) shift_register_4 (
    .shift(Shift), .in(shift_register_3_out), .clk(Clock), .q0(out_2[0]));  // open: out, load, clr, d0
  Counter #(.width(3), .max('h7)) counter_1 (.clk(Clock));  // open: load, D, count, Q, carry, clr
  xor xor_1 (xor_1_out, out_2[0], out_2[1]);
  Counter #(.width(1), .max('h1)) counter_2 (
    .count(xor_1_out), .Q(counter_2_q), .clk(Clock));  // open: load, D, carry, clr
  not not_2 (not_2_out, xor_1_out);
  Clock clock_1 (.out(Clock));
  or or_1 (Shift, counter_2_q, not_2_out);

  // Notes on the sheet:
  //   BR
  //   AC
  //   Qn
  //   QR
  //   Q(n+1)
  //   SC
endmodule
