// Logisim project commonBusArchitecture.circ as structural Verilog: 1 circuit, main circuit main
module main (
  input  [3:0] in_1,
  input  [3:0] in_2,
  input  [3:0] in_3,
  input  [3:0] in_4,
  input  in_5,
  input  in_6,
  input  in_7,
  input  in_8,
  input  in_9,
  input  in_10,
  input  in_11,
  input  in_12,
  input  in_13,
  input  in_14,
  input  in_15,
  input  in_16,
  input  in_17,
  input  in_18,
  input  in_19,
  input  in_20,
  input  [1:0] in_21,
  input  [1:0] in_22,
  output out_23,
  output out_24,
  output out_25,
  output out_26,
  output out_27,
  output out_28,
  output out_29,
  output out_30
);

  wire clock_1_out;
  wire [3:0] register_1_q, register_2_q, register_3_q, register_4_q;

  Multiplexer #(.select(2)) multiplexer_1 (
    .in0(in_5), .in1(in_9), .in2(in_13), .in3(in_17), .out(out_23), .sel(in_21));  // open: en
  Multiplexer #(.select(2)) multiplexer_2 (
    .in0(in_6), .in1(in_10), .in2(in_14), .in3(in_18), .out(out_24), .sel(in_21));  // open: en
  Multiplexer #(.select(2)) multiplexer_3 (
    .in0(in_7), .in1(in_11), .in2(in_15), .in3(in_19), .out(out_25), .sel(in_21));  // open: en
  Multiplexer #(.select(2)) multiplexer_4 (
    .in0(in_8), .in1(in_12), .in2(in_16), .in3(in_20), .out(out_26), .sel(in_21));  // open: en
  Clock clock_1 (.out(clock_1_out));
  Register #(.width(4)) register_1 (.D(in_1), .Q(register_1_q), .clk(clock_1_out));  // open: en, clr
  Multiplexer #(.select(2)) multiplexer_5 (
    .in0(register_1_q[0]), .in1(register_2_q[0]), .in2(register_3_q[0]), .in3(register_4_q[0]), .out(out_27),
    .sel(in_22));  // open: en
  Register #(.width(4)) register_2 (.D(in_2), .Q(register_2_q), .clk(clock_1_out));  // open: en, clr
  Multiplexer #(.select(2)) multiplexer_6 (
    .in0(register_1_q[1]), .in1(register_2_q[1]), .in2(register_3_q[1]), .in3(register_4_q[1]), .out(out_28),
    .sel(in_22));  // open: en
  Register #(.width(4)) register_3 (.D(in_3), .Q(register_3_q), .clk(clock_1_out));  // open: en, clr
  Multiplexer #(.select(2)) multiplexer_7 (
    .in0(register_1_q[2]), .in1(register_2_q[2]), .in2(register_3_q[2]), .in3(register_4_q[2]), .out(out_29),
    .sel(in_22));  // open: en
  Register #(.width(4)) register_4 (.D(in_4), .Q(register_4_q), .clk(clock_1_out));  // open: en, clr
  Multiplexer #(.select(2)) multiplexer_8 (
    .in0(register_1_q[3]), .in1(register_2_q[3]), .in2(register_3_q[3]), .in3(register_4_q[3]), .out(out_30),
    .sel(in_22));  // open: en

  // Notes on the sheet:
  //   in_3: pull=down
  //   Common bus without clock cycles
  //   Common Bus Architecture
endmodule
