// Logisim project excess3Adder.circ as structural Verilog: 1 circuit, main circuit main
module main (
  input  in_1,
  input  in_2,
  input  in_3,
  input  in_4,
  input  in_5,
  input  in_6,
  input  in_7,
  input  in_8,
  input  in_9,
  input  in_10,
  input  in_11,
  input  in_12,
  input  in_13,
  output out_14,
  output out_15,
  output out_16,
  output out_17,
  output out_18
);

  wire adder_1_cout, adder_1_out, adder_2_cout, adder_3_cout, adder_3_out, adder_4_cout, adder_5_cout,
       adder_5_out, adder_6_cout, adder_7_cout, adder_7_out, adder_8_cout;

  Adder #(.width(1)) adder_1 (.a(in_4), .b(in_8), .out(adder_1_out), .cin(in_9), .cout(adder_1_cout));
  Adder #(.width(1)) adder_2 (.a(adder_1_out), .b(in_10), .out(out_18), .cout(adder_2_cout));  // open: cin
  Adder #(.width(1)) adder_3 (.a(in_3), .b(in_7), .out(adder_3_out), .cin(adder_1_cout), .cout(adder_3_cout));
  Adder #(.width(1)) adder_4 (.a(adder_3_out), .b(in_11), .out(out_17), .cin(adder_2_cout), .cout(adder_4_cout));
  Adder #(.width(1)) adder_5 (.a(in_2), .b(in_6), .out(adder_5_out), .cin(adder_3_cout), .cout(adder_5_cout));
  Adder #(.width(1)) adder_6 (.a(adder_5_out), .b(in_12), .out(out_16), .cin(adder_4_cout), .cout(adder_6_cout));
  Adder #(.width(1)) adder_7 (.a(in_1), .b(in_5), .out(adder_7_out), .cin(adder_5_cout), .cout(adder_7_cout));
  Adder #(.width(1)) adder_8 (.a(adder_7_out), .b(in_13), .out(out_15), .cin(adder_6_cout), .cout(adder_8_cout));
  and and_1 (out_14, adder_8_cout, adder_7_cout);
endmodule
