// Logisim project excess3AdderOptimized.circ as structural Verilog: 1 circuit, main circuit main
module main (
  input  [3:0] in_1,
  input  [3:0] in_2,
  input  [3:0] in_3,
  output [3:0] out_4,
  output out_5
);

  wire adder_1_cout, adder_2_cout;
  wire [3:0] adder_1_out;

  Adder #(.width(4)) adder_1 (.a(in_1), .b(in_3), .out(adder_1_out), .cout(adder_1_cout));  // open: cin
  Adder #(.width(4)) adder_2 (.a(adder_1_out), .b(in_2), .out(out_4), .cout(adder_2_cout));  // open: cin
  and and_1 (out_5, adder_2_cout, adder_1_cout);
endmodule
