// Logisim project fetchCycle.circ as structural Verilog: 1 circuit, main circuit main
module main (
);

  wire button_1_out, clock_1_out, counter_1_q, not_1_out, not_2_out;
  wire [11:0] counter_2_q, register_1_q;
  wire [15:0] ram_1_data;

  Clock clock_1 (.out(clock_1_out));
  Counter #(.width(1), .max('h1)) counter_1 (.Q(counter_1_q), .clk(clock_1_out));  // open: load, D, count, carry, clr
  Register #(.width(12)) register_1 (
    .D(counter_2_q), .en(not_1_out), .Q(register_1_q), .clk(clock_1_out), .clr(button_1_out));
  not not_1 (not_1_out, counter_1_q);
  Counter #(.width(12), .max('hfff)) counter_2 (
    .count(counter_1_q), .Q(counter_2_q), .clk(clock_1_out), .clr(button_1_out));  // open: load, D, carry
  not not_2 (not_2_out, counter_1_q);
  Button button_1 (.out(button_1_out));
  Register #(.width(16)) register_2 (.D(ram_1_data), .en(not_2_out), .clk(clock_1_out), .clr(button_1_out));  // open: Q
  RAM #(.addrWidth(12), .dataWidth(16)) ram_1 (
    .addr(register_1_q), .data(ram_1_data), .clk(clock_1_out));  // open: sel, ld, clr

  // Notes on the sheet:
  //   AR
  //   PC
endmodule
