// Logisim project fullAdder.circ as structural Verilog: 1 circuit, main circuit main
module main (
  input  X,
  input  Y,
  input  Z,
  output Sum,
  output Carry
);

  wire and_1_out, and_2_out, xor_1_out;

  xor xor_1 (xor_1_out, X, Y);
  and and_1 (and_1_out, X, Y);
  and and_2 (and_2_out, xor_1_out, Z);
  xor xor_2 (Sum, xor_1_out, Z);
  or or_1 (Carry, and_1_out, and_2_out);
endmodule
