// Logisim project fullAdderUsingNANDGates.circ as structural Verilog: 1 circuit, main circuit main
module main (
  input  X,
  input  Y,
  input  Z,
  output S,
  output C
);

  wire nand_1_out, nand_2_out, nand_3_out, nand_4_out, nand_5_out, nand_6_out, nand_8_out, nand_9_out,
       nand_10_out, nand_11_out;

  nand nand_1 (nand_1_out, X, Y);
  nand nand_2 (nand_2_out, X, nand_1_out);
  nand nand_3 (nand_3_out, nand_1_out, Y);
  nand nand_4 (nand_4_out, Y, X);
  nand nand_5 (nand_5_out, X, Z);
  nand nand_6 (nand_6_out, Y, Z);
  nand nand_7 (C, nand_4_out, nand_5_out, nand_6_out);
  nand nand_8 (nand_8_out, nand_2_out, nand_3_out);
  nand nand_9 (nand_9_out, nand_8_out, Z);
  nand nand_10 (nand_10_out, nand_8_out, nand_9_out);
  nand nand_11 (nand_11_out, nand_9_out, Z);
  nand nand_12 (S, nand_10_out, nand_11_out);
endmodule
