// Logisim project fullSubtractorsUsingShiftRegisters.circ as structural Verilog: 1 circuit, main circuit main
module main (
  input  in_1,
  input  in_2,
  input  in_3,
  input  in_4,
  input  in_5,
  input  in_6
);

  wire adder_1_cout, adder_1_out, and_1_out, and_2_out, clock_1_out, clock_2_out, d_ff_1_q, d_ff_2_q,
       shift_register_1_out, shift_register_2_out, shift_register_3_out, shift_register_4_out,
       subtractor_1_bout, subtractor_1_out;

  Clock clock_1 (.out(clock_1_out));
  Clock clock_2 (.out(clock_2_out));
  Shift_Register #(.length(4)) shift_register_1 (
    .shift(in_4), .in(subtractor_1_out), .clk(clock_1_out), .out(shift_register_1_out));  // open: load, clr, d0, q0, d1, q1, d2, q2, d3, q3
  Shift_Register #(.length(4)) shift_register_2 (
    .shift(in_4), .in(in_5), .clk(clock_1_out), .out(shift_register_2_out));  // open: load, clr, d0, q0, d1, q1, d2, q2, d3, q3
  Shift_Register #(.length(4)) shift_register_3 (
    .shift(in_1), .in(adder_1_out), .clk(clock_2_out), .out(shift_register_3_out));  // open: load, clr, d0, q0, d1, q1, d2, q2, d3, q3
  Shift_Register #(.length(4)) shift_register_4 (
    .shift(in_1), .in(in_2), .clk(clock_2_out), .out(shift_register_4_out));  // open: load, clr, d0, q0, d1, q1, d2, q2, d3, q3
  and and_1 (and_1_out, in_4, clock_1_out);
  and and_2 (and_2_out, in_1, clock_2_out);
  Subtractor #(.width(1)) subtractor_1 (
    .a(shift_register_1_out), .b(shift_register_2_out), .out(subtractor_1_out), .bin(d_ff_1_q),
    .bout(subtractor_1_bout));
  D_Flip_Flop d_ff_1 (.clk(and_1_out), .D(subtractor_1_bout), .Q(d_ff_1_q), .reset(in_6));  // open: Qn, preset, en
  Adder #(.width(1)) adder_1 (
    .a(shift_register_3_out), .b(shift_register_4_out), .out(adder_1_out), .cin(d_ff_2_q), .cout(adder_1_cout));
  D_Flip_Flop d_ff_2 (.clk(and_2_out), .D(adder_1_cout), .Q(d_ff_2_q), .reset(in_3));  // open: Qn, preset, en

  // Notes on the sheet:
  //   Full-Subtrator Using Shift Registers and adder
  //   Full-Subtractor using Shift Registers and subtractor
endmodule
