// Logisim project serialCommonBusArchitecture.circ as structural Verilog: 1 circuit, main circuit main
module main (
  input  [1:0] in_1
);

  wire clock_1_out, multiplexer_1_out, shift_register_1_out, shift_register_2_out, shift_register_3_out,
       shift_register_4_out;

  Clock clock_1 (.out(clock_1_out));
  Shift_Register #(.length(4)) shift_register_1 (
    .in(multiplexer_1_out), .clk(clock_1_out), .out(shift_register_1_out));  // open: shift, load, clr, d0, q0, d1, q1, d2, q2, d3, q3
  Shift_Register #(.length(4)) shift_register_2 (
    .clk(clock_1_out), .out(shift_register_2_out));  // open: shift, in, load, clr, d0, q0, d1, q1, d2, q2, d3, q3
  Shift_Register #(.length(4)) shift_register_3 (
    .clk(clock_1_out), .out(shift_register_3_out));  // open: shift, in, load, clr, d0, q0, d1, q1, d2, q2, d3, q3
  Shift_Register #(.length(4)) shift_register_4 (
    .clk(clock_1_out), .out(shift_register_4_out));  // open: shift, in, load, clr, d0, q0, d1, q1, d2, q2, d3, q3
  Multiplexer #(.select(2)) multiplexer_1 (
    .in0(shift_register_1_out), .in1(shift_register_2_out), .in2(shift_register_3_out),
    .in3(shift_register_4_out), .out(multiplexer_1_out), .sel(in_1));  // open: en
endmodule
